// Logisim project FlipFlop-D_Example.circ as structural Verilog: 1 circuit, main circuit main
module main (
  input  Clock,
  input  X,
  output out_3,
  output out_4
);

  D_Flip_Flop d_ff_1 (.clk(Clock), .D(X), .Q(out_3), .Qn(out_4));  // open: preset, en, reset
endmodule
