// Logisim project FlipFlop-JK_Example.circ as structural Verilog: 1 circuit, main circuit main
module main (
  input  in_1,
  input  in_2,
  input  in_3,
  output out_4,
  output out_5
);

  J_K_Flip_Flop j_k_ff_1 (.J(in_1), .clk(in_2), .K(in_3), .Q(out_4), .Qn(out_5));  // open: preset, en, reset
endmodule
